// Logisim project carwindow.circ as structural Verilog: 1 circuit, main circuit main
module main (
  input  i1,
  input  i0,
  output s2,
  output s1,
  output s0
);

  wire and_1_out, and_2_out, and_3_out, and_4_out, and_5_out, and_6_out, and_7_out, and_8_out, and_9_out,
       and_10_out, and_11_out, and_12_out, and_13_out, and_14_out, and_15_out, and_16_out, and_17_out,
       and_18_out, clock_1_out, not_1_out, not_2_out, not_3_out, not_4_out, not_5_out, or_1_out, or_2_out,
       or_3_out, or_4_out, or_5_out, or_6_out, or_7_out, or_8_out, or_9_out;

  not not_1 (not_1_out, i1);
  not not_2 (not_2_out, i0);
  not not_3 (not_3_out, s2);
  not not_4 (not_4_out, s1);
  not not_5 (not_5_out, s0);
  and and_1 (and_1_out, not_1_out, s2);
  and and_2 (and_2_out, i0, s2);
  and and_3 (and_3_out, i1, s0);
  and and_4 (and_4_out, not_2_out, s1);
  and and_5 (and_5_out, not_1_out, s0);
  and and_6 (and_6_out, s1, not_5_out);
  and and_7 (and_7_out, i1, s2);
  and and_8 (and_8_out, not_1_out, not_3_out);
  and and_9 (and_9_out, i1, s1);
  and and_10 (and_10_out, and_3_out, not_4_out);
  and and_11 (and_11_out, and_5_out, not_2_out);
  and and_12 (and_12_out, and_6_out, i1);
  and and_13 (and_13_out, and_5_out, s1);
  and and_14 (and_14_out, and_7_out, not_2_out);
  and and_15 (and_15_out, and_8_out, i0);
  and and_16 (and_16_out, and_9_out, not_2_out);
  and and_17 (and_17_out, and_4_out, i1);
  and and_18 (and_18_out, i0, and_10_out);
  or or_1 (or_1_out, and_1_out, and_2_out);
  or or_2 (or_2_out, and_4_out, and_11_out);
  or or_3 (or_3_out, and_15_out, and_16_out);
  or or_4 (or_4_out, and_12_out, or_2_out);
  or or_5 (or_5_out, or_3_out, and_17_out);
  or or_6 (or_6_out, and_18_out, or_1_out);
  or or_7 (or_7_out, or_4_out, and_13_out);
  or or_8 (or_8_out, or_7_out, and_14_out);
  or or_9 (or_9_out, and_14_out, or_5_out);
  Register #(.width(1)) register_1 (.D(or_6_out), .en(1'b1), .Q(s2), .clk(clock_1_out));  // open: clr
  Register #(.width(1)) register_2 (.D(or_8_out), .en(1'b1), .Q(s1), .clk(clock_1_out));  // open: clr
  Register #(.width(1)) register_3 (.D(or_9_out), .en(1'b1), .Q(s0), .clk(clock_1_out));  // open: clr
  Clock clock_1 (.out(clock_1_out));
endmodule
